# Fritzing sketch wemos and rgb led (saved by Fritzing 0.9.3b)

parts:
  WeMos_D1_Mini1 = WeMos D1 Mini
  R1 = Resistor [tolerance=±5% resistance=1k package=THT]
  LED1 = RGB LED - (4 legs) [package="5 mm [THT]"]
  R2 = Resistor [tolerance=±5% resistance=1k package=THT]
  R3 = Resistor [tolerance=±5% resistance=1k package=THT]

nets:
  N1: WeMos_D1_Mini1.3V3, LED1.common_anode
  N2: WeMos_D1_Mini1.D6, R1.Pin_1
  N3: WeMos_D1_Mini1.D7, R2.Pin_1
  N4: WeMos_D1_Mini1.D8, R3.Pin_1
  N5: R1.Pin_0, LED1.red_cathode
  N6: LED1.green_cathode, R2.Pin_0
  N7: LED1.blue_cathode, R3.Pin_0
